# Fritzing sketch RBOT (saved by Fritzing 0.9.3b)
breadboards: 1

parts:
  Part1 = Arduino Mega 2560 (Rev3)
  Pololu_A1 = Pololu A4988 [package=SO16]
  RHT1 = Humidity and Temperature Sensor RHT03
  Grove1 = Grove Light Sensor
  Grove2 = Grove Temperature Sensor
  LED5 = Super Flux RGB LED (com. anode)
  U1 = LCD-16X2 [package=lcd-16x2_noholes]
  M3 = Stepper Motor - Bipolar
  Part2 = Bluetooth HC-05 Macho
  I2C_LCD_Backpack1 = I2C LCD Backpack [chip_label="I2C LCD Backpack" package="SIP (Single Inline) [THT]"]
  C1 = Electrolytic Capacitor [capacitance=100μF package="0807 [SMD, electrolytic]"]
  C2 = Electrolytic Capacitor [capacitance=100μF package="0807 [SMD, electrolytic]"]
  Servo_1 = Servo 1
  Servo_3 = Servo 3
  Servo_4 = Servo 4
  Servo_5 = Servo 5
  Servo_6 = Servo 6
  Servo_7 = Servo 6
  Servo_8 = Servo 6
  Servo_2 = Servo 2
  Pololu_A2 = Pololu A4988 [package=SO16]
  M4 = Stepper Motor - Bipolar
  hc-sr1 = hc-sr04
  LED6 = Super Flux RGB LED (com. anode)

nets (from the schematic view):
  N1: Part1.A1, Grove2.SIG
  N2: Part1.A2, Grove1.SIG
  N3: Part1.D21/SCL, I2C_LCD_Backpack1.SCL
  N4: Part1.D20/SDA, I2C_LCD_Backpack1.SDA
  GND: Part1.GND, RHT1.GND_1, Part2.GND, I2C_LCD_Backpack1.GND, C1.-, C2.-, Servo_1.gnd, Servo_3.gnd, Servo_4.gnd, Servo_5.gnd, Servo_6.gnd, Servo_7.gnd, Servo_8.gnd, Servo_2.gnd, Pololu_A2.GND, hc-sr1.GND
  N5: Part1.D11_PWM, LED5.red_cathode
  N6: Part1.D10_PWM, LED5.blue_cathode
  N7: Part1.D9_PWM, LED5.green_cathode
  N8: Part1.D8_PWM, LED6.green_cathode
  N9: Part1.D0_RX0, Part2.TXD
  N10: Part1.D1_TX0, Part2.RXD
  N11: Part1.D2_PWM, Servo_4.pulse
  N12: Part1.D3_PWM, Servo_5.pulse
  N13: Part1.D4_PWM, Servo_3.pulse
  N14: Part1.D5_PWM, Servo_1.pulse
  N15: Part1.D6_PWM, LED6.red_cathode
  N16: Part1.D7_PWM, LED6.blue_cathode
  N17: Part1.D28, Servo_6.pulse
  N18: Part1.D30, Servo_7.pulse
  N19: Part1.D32, Servo_2.pulse
  N20: Part1.D35, hc-sr1.Trig
  N21: Part1.D36, Pololu_A2.DIR
  N22: Part1.D37, Pololu_A2.STEP
  N23: Part1.D38, Pololu_A1.DIR
  N24: Part1.D39, Pololu_A1.STEP
  N25: Part1.D40, Pololu_A2.SLEEP
  N26: Part1.D41, Pololu_A1.SLEEP
  N27: Part1.D45, RHT1.Data-signal
  N28: Part1.D51, Servo_8.pulse
  N29: Part1.D52, hc-sr1.Echo
  GND_2: Pololu_A1.GND, RHT1.GND_2, Grove1.GND, Grove2.GND
  VCC: Pololu_A1.VDD, RHT1.Vcc, Grove1.VCC, Grove2.VCC, LED5.common_anode, Part2.VCC, I2C_LCD_Backpack1.VCC, Servo_8.vcc, Pololu_A2.VDD, hc-sr1.VCC, LED6.common_anode
  N30: Pololu_A1.1B, M3.C
  N31: Pololu_A1.1A, M3.A
  N32: Pololu_A1.2A, M3.B
  N33: Pololu_A1.2B, M3.D
  N34: U1.VSS, I2C_LCD_Backpack1.connector4
  N35: U1.VDD, I2C_LCD_Backpack1.connector5
  N36: U1.VO, I2C_LCD_Backpack1.connector6
  N37: U1.RS, I2C_LCD_Backpack1.connector7
  N38: U1.R_W, I2C_LCD_Backpack1.connector8
  N39: U1.E, I2C_LCD_Backpack1.connector9
  N40: U1.DB0, I2C_LCD_Backpack1.connector10
  N41: U1.DB1, I2C_LCD_Backpack1.connector11
  N42: U1.DB2, I2C_LCD_Backpack1.connector12
  N43: U1.DB3, I2C_LCD_Backpack1.connector13
  N44: U1.DB4, I2C_LCD_Backpack1.connector14
  N45: U1.DB5, I2C_LCD_Backpack1.connector15
  N46: U1.DB6, I2C_LCD_Backpack1.connector16
  N47: U1.DB7, I2C_LCD_Backpack1.connector17
  N48: U1.A, I2C_LCD_Backpack1.connector18
  N49: U1.K, I2C_LCD_Backpack1.connector19
  VCC_2: C1.+, Servo_1.vcc, Servo_3.vcc, Servo_4.vcc, Servo_6.vcc, Servo_2.vcc
  VCC_3: C2.+, Servo_5.vcc, Servo_7.vcc
  N50: Pololu_A2.1B, M4.C
  N51: Pololu_A2.1A, M4.A
  N52: Pololu_A2.2A, M4.B
  N53: Pololu_A2.2B, M4.D

custom parts:
  Servo 1: A generic servo.
  Servo 3: A generic servo.
  Servo 4: A generic servo.
  Servo 5: A generic servo.
  Servo 6: A generic servo.
  Servo 2: A generic servo.
